# Fritzing sketch standuino (saved by Fritzing 0.9.2b)
breadboards: 1

parts:
  Part2 = Arduino Pro Mini v13
  LED1 = LED - 5mm [color="Green (555nm)" package="5 mm [THT]"]
  R1 = Resistor [tolerance=±5% resistance=220 package=THT]
  Part1 = Seven-Segment LED Backpack 1.2 Inch Digits [part_number=1268]
  R2 = Resistor [tolerance=±5% resistance=220 package=THT]
  LED2 = LED - 5mm [color="Red (633nm)" package="5 mm [THT]"]
  LED3 = LED - 5mm [color="Yellow (585nm)" package="5 mm [THT]"]
  LED4 = LED - 5mm [color="Blue (430nm)" package="5 mm [THT]"]
  R4 = Resistor [tolerance=±5% resistance=220 package=THT]
  R5 = Resistor [tolerance=±5% resistance=220 package=THT]
  LED5 = LED - 5mm [color="White (6500K)" package="5 mm [THT]"]
  R3 = Resistor [tolerance=±5% resistance=220 package=THT]
  IR1 = TSOP312.., 314.. [package=THT]
  S2 = Toggle Switch [package=THT]
  BAT1 = BC9VPC [package=bc9vpc]

nets:
  VCC: Part2.VCC, Part1.VDD, Part1.VCCIO, IR1.Vs
  GND: Part2.GND, R1.Pin_0, Part1.GND, R2.Pin_0, R4.Pin_0, R5.Pin_0, R3.Pin_0, IR1.GND, BAT1.V-
  N1: Part2.A4, Part1.SDA
  N2: Part2.A5, Part1.SCL
  N3: Part2.RAW, S2.L1
  N4: Part2.D10_PWM/SS, IR1.Data
  N5: Part2.D9_PWM, LED1.anode
  N6: Part2.D8, LED2.anode
  N7: Part2.D7, LED3.anode
  N8: Part2.D6_PWM, LED4.anode
  N9: Part2.D5_PWM, LED5.anode
  N10: LED1.cathode, R1.Pin_1
  N11: R2.Pin_1, LED2.cathode
  N12: LED3.cathode, R3.Pin_1
  N13: LED4.cathode, R4.Pin_1
  N14: R5.Pin_1, LED5.cathode
  N15: S2.COM, BAT1.V+

custom parts:
  Seven-Segment LED Backpack 1.2 Inch Digits: This jumbo 1.2" 7-segment LED display includes a driver chip for simple control via an I2C interface. The backpack features address-selection jumpers so you can connect up to eight displays on a single I2C bus.
